// Logisim project main.circ as structural Verilog: 7 circuits, main circuit main
module main (
);

  wire clear_out, clock_1_out, controller_1_alu_s0, controller_1_d_rd, controller_1_d_wr, controller_1_fetch,
       controller_1_rf_rp_rd, controller_1_rf_rq_rd, controller_1_rf_s, controller_1_rf_w_wr;
  wire [3:0] controller_1_rf_rp_addr, controller_1_rf_rq_addr, controller_1_rf_w_addr;
  wire [7:0] controller_1_d_addr;
  wire [15:0] alu_1_output, ir_1_output, multiplexer_1_out, n256x16_1_r_data, pc_1_addr, rf_1_rp_data,
       rf_1_rq_data, rom_1_data;

  Button clear (.out(clear_out));
  Clock clock_1 (.out(clock_1_out));
  PC pc_1 (.Clk(clock_1_out), .reset(clear_out), .up(controller_1_fetch), .addr(pc_1_addr));
  ROM #(.addrWidth(16), .dataWidth(16)) rom_1 (.addr(pc_1_addr), .data(rom_1_data));  // open: sel
  IR ir_1 (.data(rom_1_data), .clk(clock_1_out), .ld(controller_1_fetch), .\output (ir_1_output));
  Controller controller_1 (
    .\input (ir_1_output), .clk(clock_1_out), .D_addr(controller_1_d_addr),
    .RF_Rq_addr(controller_1_rf_rq_addr), .RF_Rp_addr(controller_1_rf_rp_addr),
    .RF_W_addr(controller_1_rf_w_addr), .D_rd(controller_1_d_rd), .RF_s(controller_1_rf_s),
    .D_wr(controller_1_d_wr), .alu_s0(controller_1_alu_s0), .RF_W_wr(controller_1_rf_w_wr),
    .RF_Rq_rd(controller_1_rf_rq_rd), .RF_Rp_rd(controller_1_rf_rp_rd), .fetch(controller_1_fetch));
  _256x16 u_256x16_1 (
    .wr(controller_1_d_wr), .D_addr(controller_1_d_addr), .clk(clock_1_out), .rd(controller_1_d_rd),
    .R_data(n256x16_1_r_data), .W_data(rf_1_rp_data));
  Multiplexer #(.width(16)) multiplexer_1 (
    .in0(n256x16_1_r_data), .in1(alu_1_output), .out(multiplexer_1_out), .sel(controller_1_rf_s));  // open: en
  RF rf_1 (
    .W_data(multiplexer_1_out), .RF_W_addr(controller_1_rf_w_addr), .RF_W_wr(controller_1_rf_w_wr),
    .RF_Rp_adr(controller_1_rf_rp_addr), .RF_Rq_adr(controller_1_rf_rq_addr), .clk(clock_1_out),
    .Rp_data(rf_1_rp_data), .Rp_rd(controller_1_rf_rp_rd), .Rq_data(rf_1_rq_data),
    .Rq_rd(controller_1_rf_rq_rd));
  ALU alu_1 (.s0(controller_1_alu_s0), .Rp(rf_1_rp_data), .Rq(rf_1_rq_data), .\output (alu_1_output));

  // Notes on the sheet:
  //   Instructions
  //   contents of rom_1 (hex, n*v repeats v):
  //   3000 0 101 2201 1202 2201 1202
  //   ROM
endmodule

module PC (
  input  up,
  input  Clk,
  input  reset,
  output [15:0] addr
);

  wire [15:0] adder_1_out;

  Register #(.width(16)) register_1 (.D(adder_1_out), .en(up), .Q(addr), .clk(Clk), .clr(reset));
  Adder #(.width(16)) adder_1 (.a(addr), .b(16'h1), .out(adder_1_out));  // open: cin, cout
endmodule

module IR (
  input  [15:0] data,
  input  clk,
  input  ld,
  output [15:0] \output 
);

  Register #(.width(16)) register_1 (.D(data), .en(ld), .Q(\output ), .clk(clk));  // open: clr
endmodule

module Controller (
  input  [15:0] \input ,
  input  clk,
  output [7:0] D_addr,
  output [3:0] RF_Rq_addr,
  output [3:0] RF_Rp_addr,
  output [3:0] RF_W_addr,
  output D_rd,
  output D_wr,
  output RF_s,
  output alu_s0,
  output RF_W_wr,
  output RF_Rq_rd,
  output RF_Rp_rd,
  output fetch
);

  wire [1:0] multiplexer_1_out, register_1_q;

  Multiplexer #(.select(2), .width(2)) multiplexer_1 (
    .in0(2'b01), .in1(2'b00), .in2(2'b00), .in3(2'b00), .out(multiplexer_1_out), .sel(register_1_q));  // open: en
  Register #(.width(2)) register_1 (.D(multiplexer_1_out), .Q(register_1_q), .clk(clk));  // open: en, clr
  Decoder #(.select(4)) decoder_1 (
    .out0(D_rd), .out1(D_wr), .out2(alu_s0), .sel(\input [15:12]));  // open: out3, out4, out5, out6, out7, out8, out9, out10, out11, out12, out13, out14, out15, en
  nor nor_1 (fetch, register_1_q[0], register_1_q[1]);
  Multiplexer #(.width(4)) multiplexer_2 (
    .in0(\input [7:4]), .in1(\input [11:8]), .out(RF_Rp_addr), .sel(D_wr));  // open: en
  or or_1 (RF_W_wr, D_rd, alu_s0);
  or or_2 (RF_Rp_rd, D_wr, alu_s0);

  assign D_addr = \input [7:0];
  assign RF_Rq_addr = \input [3:0];
  assign RF_Rq_rd = RF_Rp_rd;
  assign RF_s = alu_s0;
  assign RF_W_addr = \input [11:8];

  // Notes on the sheet:
  //   0011 = start
  //   0000 = load
  //   0001 = store
  //   0010 = add
endmodule

module RF (
  input  [15:0] W_data,
  input  [3:0] RF_W_addr,
  input  RF_W_wr,
  input  Rp_rd,
  input  [3:0] RF_Rp_adr,
  input  Rq_rd,
  input  [3:0] RF_Rq_adr,
  input  clk,
  output [15:0] Rp_data,
  output [15:0] Rq_data
);

  wire button_1_out, button_2_out, button_3_out, button_4_out, decoder_1_out0, decoder_1_out1,
       decoder_1_out2, decoder_1_out3, decoder_1_out4, decoder_1_out5, decoder_1_out6, decoder_1_out7,
       decoder_1_out8, decoder_1_out9, decoder_1_out10, decoder_1_out11, decoder_1_out12, decoder_1_out13,
       decoder_1_out14, decoder_1_out15;
  wire [15:0] register_1_q, register_2_q, register_3_q, register_4_q, register_5_q, register_6_q,
       register_7_q, register_8_q, register_9_q, register_10_q, register_11_q, register_12_q, register_13_q,
       register_14_q, register_15_q, register_16_q;

  Decoder #(.select(4)) decoder_1 (
    .out0(decoder_1_out0), .out1(decoder_1_out1), .out2(decoder_1_out2), .out3(decoder_1_out3),
    .out4(decoder_1_out4), .out5(decoder_1_out5), .out6(decoder_1_out6), .out7(decoder_1_out7),
    .out8(decoder_1_out8), .out9(decoder_1_out9), .out10(decoder_1_out10), .out11(decoder_1_out11),
    .out12(decoder_1_out12), .out13(decoder_1_out13), .out14(decoder_1_out14), .out15(decoder_1_out15),
    .sel(RF_W_addr), .en(RF_W_wr));
  Register #(.width(16)) register_1 (.D(W_data), .en(decoder_1_out0), .Q(register_1_q), .clk(clk), .clr(button_1_out));
  Button button_1 (.out(button_1_out));
  Register #(.width(16)) register_2 (.D(W_data), .en(decoder_1_out1), .Q(register_2_q), .clk(clk), .clr(button_2_out));
  Button button_2 (.out(button_2_out));
  Register #(.width(16)) register_3 (.D(W_data), .en(decoder_1_out2), .Q(register_3_q), .clk(clk), .clr(button_3_out));
  Button button_3 (.out(button_3_out));
  Register #(.width(16)) register_4 (.D(W_data), .en(decoder_1_out3), .Q(register_4_q), .clk(clk), .clr(button_4_out));
  Button button_4 (.out(button_4_out));
  Register #(.width(16)) register_5 (.D(W_data), .en(decoder_1_out4), .Q(register_5_q), .clk(clk));  // open: clr
  Register #(.width(16)) register_6 (.D(W_data), .en(decoder_1_out5), .Q(register_6_q), .clk(clk));  // open: clr
  Register #(.width(16)) register_7 (.D(W_data), .en(decoder_1_out6), .Q(register_7_q), .clk(clk));  // open: clr
  Register #(.width(16)) register_8 (.D(W_data), .en(decoder_1_out7), .Q(register_8_q), .clk(clk));  // open: clr
  Register #(.width(16)) register_9 (.D(W_data), .en(decoder_1_out8), .Q(register_9_q), .clk(clk));  // open: clr
  Register #(.width(16)) register_10 (.D(W_data), .en(decoder_1_out9), .Q(register_10_q), .clk(clk));  // open: clr
  Register #(.width(16)) register_11 (.D(W_data), .en(decoder_1_out10), .Q(register_11_q), .clk(clk));  // open: clr
  Register #(.width(16)) register_12 (.D(W_data), .en(decoder_1_out11), .Q(register_12_q), .clk(clk));  // open: clr
  Register #(.width(16)) register_13 (.D(W_data), .en(decoder_1_out12), .Q(register_13_q), .clk(clk));  // open: clr
  Register #(.width(16)) register_14 (.D(W_data), .en(decoder_1_out13), .Q(register_14_q), .clk(clk));  // open: clr
  Register #(.width(16)) register_15 (.D(W_data), .en(decoder_1_out14), .Q(register_15_q), .clk(clk));  // open: clr
  Register #(.width(16)) register_16 (.D(W_data), .en(decoder_1_out15), .Q(register_16_q), .clk(clk));  // open: clr
  Multiplexer #(.select(4), .width(16)) multiplexer_1 (
    .in0(register_1_q), .in1(register_2_q), .in2(register_3_q), .in3(register_4_q), .in4(register_5_q),
    .in5(register_6_q), .in6(register_7_q), .in7(register_8_q), .in8(register_9_q), .in9(register_10_q),
    .in10(register_11_q), .in11(register_12_q), .in12(register_13_q), .in13(register_14_q),
    .in14(register_15_q), .in15(register_16_q), .out(Rp_data), .sel(RF_Rp_adr), .en(Rp_rd));
  Multiplexer #(.select(4), .width(16)) multiplexer_2 (
    .in0(register_1_q), .in1(register_2_q), .in2(register_3_q), .in3(register_4_q), .in4(register_5_q),
    .in5(register_6_q), .in6(register_7_q), .in7(register_8_q), .in8(register_9_q), .in9(register_10_q),
    .in10(register_11_q), .in11(register_12_q), .in12(register_13_q), .in13(register_14_q),
    .in14(register_15_q), .in15(register_16_q), .out(Rq_data), .sel(RF_Rq_adr), .en(Rq_rd));
endmodule

module _256x16 (
  input  [7:0] D_addr,
  input  [15:0] W_data,
  input  wr,
  input  clk,
  input  rd,
  output [15:0] R_data
);

  RAM #(.dataWidth(16), .bus("separate")) ram_1 (
    .addr(D_addr), .din(W_data), .data(R_data), .str(wr), .clk(clk), .ld(rd));  // open: sel, clr

  // Notes on the sheet:
  //   RAM
endmodule

module ALU (
  input  s0,
  input  [15:0] Rp,
  input  [15:0] Rq,
  output [15:0] \output 
);

  Adder #(.width(16)) adder_1 (.a(Rp), .b(Rq), .out(\output ));  // open: cin, cout
endmodule
